# Fritzing sketch NarwhAltimeter (saved by Fritzing 0.7.12b)

parts:
  BMP1 = BMP085 Breakout
  TFT1 = 1.8" TFT Display with uSD  # not connected
  GPS1 = Adafruit Ultimate GPS Breakout  # not connected
  Nano1 = Arduino Nano v3.0
  BATT1 = LiPoly Battery (1300mAh)  # not connected
  BATT2 = LiPoly Battery (1300mAh)  # not connected

nets:
  N1: BMP1.3Vo, Nano1.3V3
  N2: BMP1.SCL, Nano1.A5
  N3: BMP1.SDA, Nano1.A4
  GND: BMP1.GND, Nano1.GND

custom parts:
  BMP085 Breakout: A breakout for the BMP085 barometric pressure and temperature sensor
  1.8" TFT Display with uSD: 1.8" TFT Display with SPI control and MicroSD card
  LiPoly Battery (1300mAh): Lithium Ion Polymer Battery (1300mAh)
